// Logisim project Computer.circ as structural Verilog: 1 circuit, main circuit main
module main (
);

  wire button_1_out, clock_1_out, main_2_p3, main_2_p5, main_2_p6, main_2_p7, main_3_refresh_screen;
  wire [15:0] main_1_out_2, main_2_p1, main_2_p2, main_2_p4, main_3_program_counter_out, main_4_p6,
       main_4_p7, main_4_p8, main_4_p9, main_4_p10, main_4_p11, main_4_p12, main_4_p13, main_4_p14,
       main_4_p15, main_4_p16, main_4_p17, main_4_p18, main_4_p19, main_4_p20, main_4_p21;

  // Probe on main_3_program_counter_out
  Clock clock_1 (.out(clock_1_out));
  ReadOnlyMemory_main main_1 (.in_1(main_3_program_counter_out), .out_2(main_1_out_2));
  Button button_1 (.out(button_1_out));
  // RandomAccessMemory_main main_2: pin names not known; wires that end beside it: main_2_p1, main_2_p2, main_2_p3, main_2_p4, main_2_p5, main_2_p6, main_2_p7
  CentralProcessingUnit_main main_3 (
    .Instruction(main_1_out_2), .inMemory(main_2_p4), .Reset(button_1_out), .outMemory(main_2_p1),
    .writeMemory(main_2_p3), .addressMemory(main_2_p2), .program_counter_out(main_3_program_counter_out),
    .Clock(clock_1_out), .Refresh_Screen(main_3_refresh_screen));
  // Screen_main main_4: pin names not known; wires that end beside it: main_3_refresh_screen, button_1_out, main_2_p5, main_2_p6, main_2_p7, main_4_p6, main_4_p7, main_4_p8, main_4_p9, main_4_p10, main_4_p11, main_4_p12, main_4_p13, main_4_p14, main_4_p15, main_4_p16, main_4_p17, main_4_p18, main_4_p19, main_4_p20, main_4_p21
  DotMatrix #(.inputtype("row"), .matrixcols(16), .matrixrows(16)) dotmatrix_1 (
    .row0(main_4_p6), .row1(main_4_p7), .row2(main_4_p8), .row3(main_4_p9), .row4(main_4_p10),
    .row5(main_4_p11), .row6(main_4_p12), .row7(main_4_p13), .row8(main_4_p14), .row9(main_4_p15),
    .row10(main_4_p16), .row11(main_4_p17), .row12(main_4_p18), .row13(main_4_p19), .row14(main_4_p20),
    .row15(main_4_p21));
endmodule
